# Fritzing sketch blinken_bonken (saved by Fritzing 0.8.5b)

parts:
  Part1 = Arduino Uno (Rev3)
  R1 = Resistor [tolerance=±5% resistance=1k package="1206 [SMD]"]
  R2 = Resistor [tolerance=±5% resistance=1k package="1206 [SMD]"]
  R3 = Resistor [tolerance=±5% resistance=1k package="1206 [SMD]"]
  7SEG1 = 7-Segment LED I2C Backpack (yellow)
  R10 = Resistor [tolerance=±5% resistance=1k package="1206 [SMD]"]
  NEOPIXEL1 = Neopixel Strip -- White (60/m)
  R7 = Analog Pressure Sensor [part_number=PW073]
  R6 = Analog Pressure Sensor [part_number=PW073]
  R8 = Analog Pressure Sensor [part_number=PW073]
  R9 = Analog Pressure Sensor [part_number=PW073]

nets:
  N1: Part1.A0, R3.Pin_1, R6.pin_0
  N2: Part1.A1, R1.Pin_1, R9.pin_0
  N3: Part1.A2, R2.Pin_1, R7.pin_0
  N4: Part1.A3, R10.Pin_1, R8.pin_0
  GND: Part1.GND, R1.Pin_0, R3.Pin_0, 7SEG1.GND, R10.Pin_0, NEOPIXEL1.GND
  N5: Part1.A4/SDA, 7SEG1.SDA
  N6: Part1.A5/SCL, 7SEG1.SCL
  N7: Part1.D6_PWM, NEOPIXEL1.+5V
  N8: Part1.5V, 7SEG1.V+, NEOPIXEL1.DI, R7.pin_1, R6.pin_1, R8.pin_1, R9.pin_1

custom parts:
  7-Segment LED I2C Backpack (yellow): 4-digit, 7-segment LED Display with I2C Control
  Neopixel Strip -- White (60/m): Neopixel Strip, White, 60 pixels per meter.
  Analog Pressure Sensor: An Analog Pressure Sensor made with wire and velostat
